# Fritzing sketch Final Schematic v1 (saved by Fritzing 1.0.4)
breadboards: 1

parts:
  Heltec_WiFi_LoRa_V3 = Heltec WiFi LoRa 32 V3 [part_number=HTIT-WB32LA]
  Accelerometer = SparkFun_LIS3DH-Breakout [part_number=LIS3DH]
  Temp_&_RH = SHT35-D [part_number=SHT35-D1 package="SIP (Single Inline) [THT]"]
  A1 = Micro SD card reader
  V1 = DC Power [voltage=5V internal_resistance=0.1Ω]
  Part1 = Adafruit NAU7802
  R1 = Resistor [tolerance=±1% resistance=360 package="0805 [SMD]"]
  R2 = Resistor [tolerance=±1% resistance=360 package="0805 [SMD]"]
  R3 = Resistor [tolerance=±1% resistance=360 package="0805 [SMD]"]
  Linear_Strain_Gauge = KFH-3-350 (strain gauge) [package="0805 [SMD]"]
  C1 = Ceramic Capacitor [capacitance=0.1µF voltage=35V package="0805 [SMD, multilayer]"]
  C2 = Electrolytic Capacitor [capacitance=10µF voltage=35V package="0807 [SMD, electrolytic]"]
  R4 = Resistor [tolerance=±5% resistance=100 package="2512 [SMD]"]
  C3 = Ceramic Capacitor [capacitance=0.1µF voltage=35V package="0805 [SMD, multilayer]"]
  C4 = Electrolytic Capacitor [capacitance=10µF voltage=35V package="0807 [SMD, electrolytic]"]
  C5 = Ceramic Capacitor [capacitance=1.5nF voltage=35V package="0805 [SMD, multilayer]"]
  C6 = Ceramic Capacitor [capacitance=1.5nF voltage=35V package="0805 [SMD, multilayer]"]

nets:
  N1: Heltec_WiFi_LoRa_V3.pin_11, Accelerometer.SDA, Temp_&_RH.SDA, Part1.SDA
  N2: Heltec_WiFi_LoRa_V3.pin_12, Accelerometer.SCL, Temp_&_RH.SCL, Part1.SCL
  3.3V: Heltec_WiFi_LoRa_V3.pin_16, Heltec_WiFi_LoRa_V3.pin_17, Accelerometer.VCC, Temp_&_RH.VDD, A1.Pin_1, Part1.VCC, R1.Pin_0, R2.Pin_0, R4.Pin_0
  GND: Heltec_WiFi_LoRa_V3.pin_18, Heltec_WiFi_LoRa_V3.pin_19, Accelerometer.GND, Temp_&_RH.GND, A1.Pin_6, V1.V-, Part1.GND, R3.Pin_1, Linear_Strain_Gauge.Pin0, C1.0, C2.-, C3.0, C4.-
  5V: Heltec_WiFi_LoRa_V3.pin_20, V1.V+, C1.1, C2.+
  N3: Heltec_WiFi_LoRa_V3.pin_27, A1.Pin_5
  N4: Heltec_WiFi_LoRa_V3.pin_28, A1.Pin_4
  N5: Heltec_WiFi_LoRa_V3.pin_29, A1.Pin_3
  N6: Heltec_WiFi_LoRa_V3.pin_30, A1.Pin_2
  N7: Part1.A+, R1.Pin_1, Linear_Strain_Gauge.Pin_1, C6.1
  N8: Part1.A-, R2.Pin_1, R3.Pin_0, C5.1
  N9: Part1.AVDD, R4.Pin_1, C3.1, C4.+
  N10: C5.0, C6.0

custom parts:
  Heltec WiFi LoRa 32 V3: The Heltec WiFi LoRa 32 is an IoT development board designed and produced by Heltec Automation and based on the Espressif ESP32-S3FN8 and Semtech SX1262 modules. The board includes WiFi, Bluetooth and LoRa functions, as well as a 0.96″ OLED display and a lithium battery management system. Links: Heltec WiFi LoRa 32 product page Github
  SparkFun_LIS3DH-Breakout: The LIS3DH Breakout is a smart, low-power, three-axis, capacitive micro-machined accelerometer with 12 bits of resolution that you can use to add translation detection to your project. It would be classified as a 3DoF, or 3 Degrees of Freedom. Inertial Measurement Units (or IMUs) can provide additional space location data, such as gyroscopic or magnetometric. The LIS3DH provided on this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
  SHT35-D: SHT35-D is an I2C connected temperature and humidity sensor
  Micro SD card reader: Micro SD card reader.
  KFH-3-350 (strain gauge): Manufacturer = Omega/Dwyer Part number = KFH-3-350-C1-11L1M2R
