# Fritzing sketch Noise Filter Circuit (saved by Fritzing 1.0.4)
breadboards: 1

parts:
  R1 = Resistor [tolerance=±5% resistance=10k package="0402 [SMD]"]
  C1 = Electrolytic Capacitor [capacitance=47nF voltage=50V package="200 mil [THT, electrolytic]"]
  C2 = Electrolytic Capacitor [capacitance=47nF voltage=50V package="200 mil [THT, electrolytic]"]
  C3 = Electrolytic Capacitor [capacitance=47nF voltage=50V package="200 mil [THT, electrolytic]"]
  R2 = Resistor [tolerance=±5% resistance=10k package="0402 [SMD]"]

nets:
  N1: R1.Pin_1, C1.+, C2.+
  GND: C1.-, C3.-
  N2: C2.-, C3.+, R2.Pin_1

notes:
  A+ (Inside Shield)
  A- (Inside Shield)
  A+ (To NAU7802)
  A- (To NAU7802)
